# Fritzing sketch Schaltplan ansicht (saved by Fritzing 0.9.3b)

parts:
  part = Adafruit DS1307 RTC Breakout [part_number="Adafruit #264"]
  Zahl4 = Neopixel Strip -- Black (30/m)
  Mittelpunkt = Neopixel Strip -- Black (30/m)
  Zahl1 = Neopixel Strip -- Black (30/m)
  Zahl2 = Neopixel Strip -- Black (30/m)
  Zahl3 = Neopixel Strip -- Black (30/m)
  Bauteil1 = Arduino Uno (Rev3)

nets:
  N1: part.SCL, Bauteil1.A5/SCL
  N2: part.SDA, Bauteil1.A4/SDA
  +5V: part.VCC, Zahl4.+5V, Mittelpunkt.+5V, Zahl1.+5V, Zahl2.+5V, Zahl3.+5V, Bauteil1.5V
  GND: part.GND, Zahl4.GND, Mittelpunkt.GND, Zahl1.GND, Zahl2.GND, Zahl3.GND, Bauteil1.GND
  N3: Zahl4.Din, Bauteil1.D10_PWM/SS
  N4: Mittelpunkt.Din, Bauteil1.D3_PWM
  N5: Zahl1.Din, Bauteil1.D5_PWM
  N6: Zahl2.Din, Bauteil1.D6_PWM
  N7: Zahl3.Din, Bauteil1.D9_PWM

notes:
  Mittel Punkte
  Zahl 1
  Zahl 2
  Zahl 3
  Zahl 4

custom parts:
  Adafruit DS1307 RTC Breakout: This is a great battery-backed real time clock (RTC) that allows your microcontroller project to keep track of time even if it is reprogrammed, or if the power is lost. Perfect for datalogging, clock-building, time stamping, timers and alarms, etc. The DS1307 is the most popular RTC - but it requires 5V power to work (although we've used it with 5V power and 3.3V logic successfully) PCB &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
  Neopixel Strip -- Black (30/m): These NeoPixel strips have 30 digitally-addressable pixel LEDs per meter and are very affordable and are only 12.5 mm wide, 10 mm if you remove the strip from the casing.
