# Fritzing sketch Steckplatine ansicht (saved by Fritzing 0.9.3b)

parts:
  Bauteil1 = Arduino Uno (Rev3)
  Bauteil2 = Adafruit DS1307 RTC Breakout [part_number="Adafruit #264"]
  NEOPIXEL3 = Neopixel Strip -- Black (30/m)
  NEOPIXEL4 = Neopixel Strip -- Black (30/m)
  NEOPIXEL5 = Neopixel Strip -- Black (30/m)
  NEOPIXEL6 = Neopixel Strip -- Black (30/m)

nets:
  N1: Bauteil1.A4/SDA, Bauteil2.SDA
  N2: Bauteil1.A5/SCL, Bauteil2.SCL
  N3: Bauteil1.D9_PWM, NEOPIXEL5.Din
  N4: Bauteil1.D10_PWM/SS, NEOPIXEL6.Din
  N5: Bauteil1.D5_PWM, NEOPIXEL3.Din
  N6: Bauteil1.D6_PWM, NEOPIXEL4.Din
  +5V: NEOPIXEL3.+5V, NEOPIXEL4.+5V
  GND: NEOPIXEL5.GND, NEOPIXEL6.GND

custom parts:
  Adafruit DS1307 RTC Breakout: This is a great battery-backed real time clock (RTC) that allows your microcontroller project to keep track of time even if it is reprogrammed, or if the power is lost. Perfect for datalogging, clock-building, time stamping, timers and alarms, etc. The DS1307 is the most popular RTC - but it requires 5V power to work (although we've used it with 5V power and 3.3V logic successfully) PCB &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
  Neopixel Strip -- Black (30/m): These NeoPixel strips have 30 digitally-addressable pixel LEDs per meter and are very affordable and are only 12.5 mm wide, 10 mm if you remove the strip from the casing.
